// Logisim project digital_clock.circ as structural Verilog: 8 circuits, main circuit gui
module gui (
);

  wire Alarm, alarm_off, alarm_t, Change, count, H, M, mode, Normal, pause, reset, S, select;
  wire [1:0] main_1_mode_view, main_1_select_view;
  wire [3:0] hd, hu, md, mu, sd, su;

  Button button_1 (.out(pause));
  Button button_2 (.out(select));
  LED led_1 (.in(H));
  Hex_Digit_Display hex_digit_display_1 (.value(hd));  // open: dp
  LED led_2 (.in(Change));
  main main_1 (
    .mode(mode), .alter(count), .select(select), .alarm_signal(alarm_t), .mode_view(main_1_mode_view),
    .view({hd, hu, md, mu, sd, su}), .pause(pause), .select_view(main_1_select_view), .time_reset(reset),
    .alarm_off(alarm_off));
  Hex_Digit_Display hex_digit_display_2 (.value(md));  // open: dp
  Hex_Digit_Display hex_digit_display_3 (.value(hu));  // open: dp
  LED led_3 (.in(M));
  Hex_Digit_Display hex_digit_display_4 (.value(mu));  // open: dp
  LED led_4 (.in(Alarm));
  Demultiplexer #(.select(2), .enable("false")) demultiplexer_1 (
    .out0(S), .out1(M), .out2(H), .in(1'b1), .sel(main_1_select_view));  // open: out3
  Demultiplexer #(.select(2), .enable("false")) demultiplexer_2 (
    .out0(Normal), .out1(Alarm), .out2(Change), .in(1'b1), .sel(main_1_mode_view));  // open: out3
  LED led_5 (.in(S));
  Hex_Digit_Display hex_digit_display_5 (.value(sd));  // open: dp
  Hex_Digit_Display hex_digit_display_6 (.value(su));  // open: dp
  LED led_6 (.in(Normal));
  LED led_7 (.in(alarm_t));
  Button button_3 (.out(mode));
  Button button_4 (.out(count));
  Button button_5 (.out(alarm_off));
  Button button_6 (.out(reset));
endmodule

// Main
module main (
  input  mode,
  input  alarm_off,
  input  pause,
  input  alter,
  input  select,
  input  time_reset,
  output [1:0] mode_view,
  output [23:0] view,
  output alarm_signal,
  output [1:0] select_view
);

  wire alarm_1_alarm_out, and_1_out, clk, counter_1_q, demultiplexer_1_out1, demultiplexer_1_out2,
       demultiplexer_2_out1, demultiplexer_2_out2, or_1_out;
  wire [23:0] alarm_1_alarm_view, timer_1_time;

  Clock clock_1 (.out(clk));
  select select_1 (.out_2(mode_view), .count(mode));
  and and_1 (and_1_out, mode_view[1], ~mode_view[0]);  // AND_Gate
  Counter #(.width(1), .max('h1)) counter_1 (.Q(counter_1_q), .clk(pause));  // open: load, D, count, carry, clr
  Demultiplexer #(.select(2), .enable("false")) demultiplexer_1 (
    .out1(demultiplexer_1_out1), .out2(demultiplexer_1_out2), .in(alter), .sel(mode_view));  // open: out0, out3
  timer timer_1 (
    .clk(clk), .\time (timer_1_time), .pause(or_1_out), .count(demultiplexer_1_out2), .select(select_view),
    .reset(demultiplexer_2_out2));
  or or_1 (or_1_out, and_1_out, counter_1_q);
  select select_2 (.out_2(select_view), .count(select));
  Multiplexer #(.select(2), .width(24), .enable("false")) multiplexer_1 (
    .in0(timer_1_time), .in1(alarm_1_alarm_view), .in2(timer_1_time), .out(view), .sel(mode_view));  // open: in3
  alarm alarm_1 (
    .select(select_view), .count(demultiplexer_1_out1), .\time (timer_1_time),
    .alarm_view(alarm_1_alarm_view), .alarm_out(alarm_1_alarm_out), .reset(demultiplexer_2_out1));
  Hex_Digit_Display hex_digit_display_1 (.value(view[19:16]));  // open: dp
  Hex_Digit_Display hex_digit_display_2 (.value(view[23:20]));  // open: dp
  D_Flip_Flop d_ff_1 (.Q(alarm_signal), .preset(alarm_1_alarm_out), .reset(alarm_off));  // open: clk, D, Qn, en
  Demultiplexer #(.select(2), .enable("false")) demultiplexer_2 (
    .out1(demultiplexer_2_out1), .out2(demultiplexer_2_out2), .in(time_reset), .sel(mode_view));  // open: out0, out3
  Hex_Digit_Display hex_digit_display_3 (.value(view[11:8]));  // open: dp
  Hex_Digit_Display hex_digit_display_4 (.value(view[15:12]));  // open: dp
  Hex_Digit_Display hex_digit_display_5 (.value(view[7:4]));  // open: dp
  Hex_Digit_Display hex_digit_display_6 (.value(view[3:0]));  // open: dp

  // Other names for the same wires on the sheet: mode_t[1:0] = mode_view
endmodule

// Timer
module timer (
  input  reset,
  input  pause,
  input  count,
  input  [1:0] select,
  input  clk,
  output [23:0] \time 
);

  wire and_1_out, demultiplexer_1_out0, demultiplexer_1_out1, demultiplexer_1_out2, dozen_1_clock_out,
       dozen_2_clock_out, hours_check_1_reset_out, or_1_out, or_2_out, or_3_out, or_4_out, unit_1_clk_out,
       unit_2_clk_out, unit_3_clk_out;

  unit unit_1 (.\output (\time [3:0]), .clk_in(or_1_out), .reset(reset), .clk_out(unit_1_clk_out));
  or or_1 (or_1_out, and_1_out, demultiplexer_1_out0);
  and and_1 (and_1_out, clk, ~pause);  // AND_Gate
  dozen dozen_1 (.\output (\time [7:4]), .clock_in(unit_1_clk_out), .reset(reset), .clock_out(dozen_1_clock_out));
  unit unit_2 (.\output (\time [11:8]), .clk_in(or_2_out), .reset(reset), .clk_out(unit_2_clk_out));
  or or_2 (or_2_out, dozen_1_clock_out, demultiplexer_1_out1);
  Demultiplexer #(.select(2), .enable("false")) demultiplexer_1 (
    .out0(demultiplexer_1_out0), .out1(demultiplexer_1_out1), .out2(demultiplexer_1_out2), .in(count),
    .sel(select));  // open: out3
  Hex_Digit_Display hex_digit_display_1 (.value(\time [23:20]));  // open: dp
  Hex_Digit_Display hex_digit_display_2 (.value(\time [19:16]));  // open: dp
  dozen dozen_2 (.\output (\time [15:12]), .clock_in(unit_2_clk_out), .reset(reset), .clock_out(dozen_2_clock_out));
  unit unit_3 (.\output (\time [19:16]), .clk_in(or_3_out), .reset(or_4_out), .clk_out(unit_3_clk_out));
  or or_3 (or_3_out, dozen_2_clock_out, demultiplexer_1_out2);
  Hex_Digit_Display hex_digit_display_3 (.value(\time [15:12]));  // open: dp
  Hex_Digit_Display hex_digit_display_4 (.value(\time [11:8]));  // open: dp
  hours_check hours_check_1 (.unit(\time [19:16]), .dozen(\time [23:20]), .reset_out(hours_check_1_reset_out));
  dozen dozen_3 (.\output (\time [23:20]), .clock_in(unit_3_clk_out), .reset(or_4_out));  // open: clock_out
  or or_4 (or_4_out, hours_check_1_reset_out, reset);
  Hex_Digit_Display hex_digit_display_5 (.value(\time [7:4]));  // open: dp
  Hex_Digit_Display hex_digit_display_6 (.value(\time [3:0]));  // open: dp
endmodule

// Alarm
module alarm (
  input  [23:0] \time ,
  input  reset,
  input  [1:0] select,
  input  count,
  output [23:0] alarm_view,
  output alarm_out
);

  wire demultiplexer_1_out0, demultiplexer_1_out1, demultiplexer_1_out2, dozen_1_clock_out,
       dozen_2_clock_out, hours_check_1_reset_out, or_1_out, or_2_out, or_3_out, unit_1_clk_out,
       unit_2_clk_out, unit_3_clk_out;

  unit unit_1 (.\output (alarm_view[3:0]), .clk_in(demultiplexer_1_out0), .reset(reset), .clk_out(unit_1_clk_out));
  dozen dozen_1 (.\output (alarm_view[7:4]), .clock_in(unit_1_clk_out), .reset(reset), .clock_out(dozen_1_clock_out));
  unit unit_2 (.\output (alarm_view[11:8]), .clk_in(or_1_out), .reset(reset), .clk_out(unit_2_clk_out));
  or or_1 (or_1_out, dozen_1_clock_out, demultiplexer_1_out1);
  Demultiplexer #(.select(2), .enable("false")) demultiplexer_1 (
    .out0(demultiplexer_1_out0), .out1(demultiplexer_1_out1), .out2(demultiplexer_1_out2), .in(count),
    .sel(select));  // open: out3
  dozen dozen_2 (.\output (alarm_view[15:12]), .clock_in(unit_2_clk_out), .reset(reset), .clock_out(dozen_2_clock_out));
  unit unit_3 (.\output (alarm_view[19:16]), .clk_in(or_2_out), .reset(or_3_out), .clk_out(unit_3_clk_out));
  or or_2 (or_2_out, dozen_2_clock_out, demultiplexer_1_out2);
  Comparator #(.width(24)) comparator_1 (.a(alarm_view), .b(\time ), .eq(alarm_out));  // open: gt, lt
  hours_check hours_check_1 (.unit(alarm_view[19:16]), .dozen(alarm_view[23:20]), .reset_out(hours_check_1_reset_out));
  dozen dozen_3 (.\output (alarm_view[23:20]), .clock_in(unit_3_clk_out), .reset(or_3_out));  // open: clock_out
  or or_3 (or_3_out, hours_check_1_reset_out, reset);
endmodule

// U
module unit (
  input  clk_in,
  input  reset,
  output [3:0] \output ,
  output clk_out
);

  wire or_1_out;
  wire [3:0] adder_1_out;

  Register #(.width(4)) register_1 (.D(adder_1_out), .Q(\output ), .clk(clk_in), .clr(or_1_out));  // open: en
  or or_1 (or_1_out, clk_out, reset);
  Adder #(.width(4)) adder_1 (.a(\output ), .b(4'b0001), .out(adder_1_out));  // open: cin, cout
  and and_1 (clk_out, ~\output [0], \output [1], ~\output [2], \output [3]);  // AND_Gate
endmodule

// D
module dozen (
  input  clock_in,
  input  reset,
  output [3:0] \output ,
  output clock_out
);

  wire or_1_out;
  wire [3:0] adder_1_out;

  Register #(.width(4)) register_1 (.D(adder_1_out), .Q(\output ), .clk(clock_in), .clr(or_1_out));  // open: en
  or or_1 (or_1_out, clock_out, reset);
  Adder #(.width(4)) adder_1 (.a(\output ), .b(4'b0001), .out(adder_1_out));  // open: cin, cout
  and and_1 (clock_out, ~\output [0], \output [1], \output [2], ~\output [3]);  // AND_Gate
endmodule

// hrs.r
module hours_check (
  input  [3:0] unit,
  input  [3:0] dozen,
  output reset_out
);

  and and_1 (reset_out, ~unit[0], ~unit[1], unit[2], ~unit[3], ~dozen[0], dozen[1]);  // AND_Gate
endmodule

// s
module select (
  input  count,
  output [1:0] out_2
);

  wire and_1_out;

  Counter #(.width(2), .max('h3)) counter_1 (.Q(out_2), .clk(count), .clr(and_1_out));  // open: load, D, count, carry
  and and_1 (and_1_out, out_2[1], out_2[0]);
endmodule
